// Logisim project Simulation.circ as structural Verilog
module Register_File (
  input  [1:0] Write_Register__RD,
  input  [1:0] Read_Register_1__RS,
  input  [15:0] Write_Data,
  input  [1:0] Read_Register_2__RS,
  input  CLK,
  input  RegWrite,
  output [15:0] Read_data_1,
  output [15:0] Read_data_2
);

  wire and_1_out, and_2_out, and_3_out, and_4_out, decoder_1_out0, decoder_1_out1, decoder_1_out2,
       decoder_1_out3;
  wire [15:0] _0_q, _1_q, _2_q, _3_q;

  Decoder #(.select(2)) decoder_1 (
    .out0(decoder_1_out0), .out1(decoder_1_out1), .out2(decoder_1_out2), .out3(decoder_1_out3),
    .sel(Write_Register__RD));  // open: en
  and and_1 (and_1_out, decoder_1_out0, RegWrite);
  and and_2 (and_2_out, decoder_1_out1, RegWrite);
  and and_3 (and_3_out, decoder_1_out2, RegWrite);
  and and_4 (and_4_out, decoder_1_out3, RegWrite);
  Register #(.width(16)) _0 (.D(Write_Data), .en(and_1_out), .Q(_0_q), .clk(CLK));  // open: clr
  Register #(.width(16)) _1 (.D(Write_Data), .en(and_2_out), .Q(_1_q), .clk(CLK));  // open: clr
  Register #(.width(16)) _2 (.D(Write_Data), .en(and_3_out), .Q(_2_q), .clk(CLK));  // open: clr
  Register #(.width(16)) _3 (.D(Write_Data), .en(and_4_out), .Q(_3_q), .clk(CLK));  // open: clr
  Multiplexer #(.select(2), .width(16)) multiplexer_1 (
    .in0(_0_q), .in1(_1_q), .in2(_2_q), .in3(_3_q), .out(Read_data_1), .sel(Read_Register_1__RS));  // open: en
  Multiplexer #(.select(2), .width(16)) multiplexer_2 (
    .in0(_0_q), .in1(_1_q), .in2(_2_q), .in3(_3_q), .out(Read_data_2), .sel(Read_Register_2__RS));  // open: en

  // Notes on the sheet:
  //   rs = rt = rd =2, 2^2 = 4 registers in register file, databits = 16 (16bit ALU)
endmodule

module _1_Bit_Alu (
  input  Cin,
  input  A,
  input  B,
  input  [1:0] Select,
  output Result,
  output out_6
);

  wire adder_1_out, and_1_out, and_2_out, multiplexer_1_out, not_1_out, or_1_out;

  not not_1 (not_1_out, B);
  and and_1 (and_1_out, A, B);
  or or_1 (or_1_out, A, B);
  Multiplexer multiplexer_1 (.in0(B), .in1(not_1_out), .out(multiplexer_1_out), .sel(and_2_out));  // open: en
  and and_2 (and_2_out, Select[0], Select[1]);
  Adder #(.width(1)) adder_1 (.a(A), .b(multiplexer_1_out), .out(adder_1_out), .cin(Cin), .cout(out_6));
  Multiplexer #(.select(2)) multiplexer_2 (
    .in0(and_1_out), .in1(or_1_out), .in2(adder_1_out), .in3(adder_1_out), .out(Result), .sel(Select));  // open: en
endmodule

module _4_Bit_Alu (
  input  Cin,
  input  [3:0] A,
  input  [3:0] B,
  input  [1:0] in_4,
  output [3:0] Result,
  output Cout
);

  wire _0_out_6, _1_out_6, _2_out_6;

  _1_Bit_Alu _0 (.Cin(Cin), .A(A[0]), .B(B[0]), .Result(Result[0]), .out_6(_0_out_6), .Select(in_4));
  _1_Bit_Alu _1 (.Cin(_0_out_6), .A(A[1]), .B(B[1]), .Result(Result[1]), .out_6(_1_out_6), .Select(in_4));
  _1_Bit_Alu _2 (.Cin(_1_out_6), .A(A[2]), .B(B[2]), .Result(Result[2]), .out_6(_2_out_6), .Select(in_4));
  _1_Bit_Alu _3 (.Cin(_2_out_6), .A(A[3]), .B(B[3]), .Result(Result[3]), .out_6(Cout), .Select(in_4));
endmodule
